// Logisim project a1-template.circ as structural Verilog: 5 circuits, main circuit main
// L1
module main (
  input  M0,
  input  E0,
  input  E1,
  input  M1
);

  wire [1:0] l0_2_lo, r0_1_ro;
  wire [4:0] rom_2_data, rom_2_data_2;
  wire [14:0] rom_1_data;
  wire [14:10] rom_2_data_3;

  L0 l0_1 ();  // open: M0, M1, E0, E1, Lo
  L0 l0_2 (.M0(M0), .M1(M1), .E0(E0), .E1(E1), .Lo(l0_2_lo[0]));
  L1 l1_1 (.M0(M0), .M1(M1), .E0(E0), .E1(E1), .L1(l0_2_lo[1]));
  R0 r0_1 (.M0(M0), .M1(M1), .E0(E0), .E1(E1), .Ro(r0_1_ro[0]));
  R1 r1_1 (.M0(M0), .M1(M1), .E0(E0), .E1(E1), .R1(r0_1_ro[1]));
  DotMatrix #(.matrixcols(3), .matrixrows(5)) dotmatrix_1 (
    .col0(rom_1_data[14:10]), .col1(rom_1_data[9:5]), .col2(rom_1_data[4:0]));
  ROM #(.addrWidth(2), .dataWidth(15)) rom_1 (.addr(l0_2_lo), .data(rom_1_data));  // open: sel
  ROM #(.addrWidth(2), .dataWidth(15)) rom_2 (
    .addr(r0_1_ro), .data({rom_2_data_3, rom_2_data_2, rom_2_data}));  // open: sel
  DotMatrix #(.matrixcols(3), .matrixrows(5)) dotmatrix_2 (.col0(rom_2_data_3), .col1(rom_2_data_2), .col2(rom_2_data));

  // Notes on the sheet:
  //   Sensors
  //   Lo decoder
  //   L1 decoder
  //   R0 decoder
  //   R1 decoder
  //   L1
  //   L0
  //   R1
  //   R0
  //   Motor Controller
  //   left
  //   contents of rom_1 (hex, n*v repeats v):
  //   1084 2308 862 288a
  //   contents of rom_2 (hex, n*v repeats v):
  //   1084 2308 862 288a
  //   right
  //   forward
  //   stopped
  //   reverse
endmodule

module L0 (
  input  M0,
  input  M1,
  input  E0,
  input  E1,
  output Lo
);

  wire and_1_out, not_1_out;

  not not_1 (not_1_out, E0);
  and and_1 (and_1_out, E0, E1);
  or or_1 (Lo, not_1_out, and_1_out);
endmodule

module L1 (
  input  M0,
  input  M1,
  input  E0,
  input  E1,
  output L1
);

  wire not_1_out;

  not not_1 (not_1_out, E1);
  and and_1 (L1, E0, not_1_out);
endmodule

module R0 (
  input  M0,
  input  M1,
  input  E0,
  input  E1,
  output Ro
);

  wire and_1_out, and_2_out, not_1_out, not_2_out;

  not not_1 (not_1_out, M0);
  not not_2 (not_2_out, E1);
  and and_1 (and_1_out, not_1_out, not_2_out);
  and and_2 (and_2_out, E0, not_2_out);
  or or_1 (Ro, and_1_out, and_2_out);
endmodule

module R1 (
  input  M0,
  input  M1,
  input  E0,
  input  E1,
  output R1
);

  wire and_1_out, and_2_out, and_3_out, not_1_out, or_1_out;

  not not_1 (not_1_out, E0);
  and and_1 (and_1_out, M0, not_1_out);
  and and_2 (and_2_out, M1, E1);
  and and_3 (and_3_out, not_1_out, E1);
  or or_1 (or_1_out, and_1_out, and_2_out);
  or or_2 (R1, or_1_out, and_3_out);
endmodule
