// Logisim project a2-template.circ as structural Verilog: 1 circuit, main circuit main
module main (
);

  wire C;
  wire [4:0] comparator_1_lt;
  wire [5:0] rom_1_data;
  wire [31:0] adder_1_out, multiplexer_1_out, multiplexer_2_out, register_1_q, register_2_q, register_3_q,
       subtractor_1_out;

  Subtractor #(.width(32)) subtractor_1 (
    .a(register_1_q), .b(register_2_q), .out(subtractor_1_out));  // open: bin, bout
  Button Reset (.out(comparator_1_lt[1]));
  Button Start (.out(comparator_1_lt[2]));
  Multiplexer #(.width(32)) multiplexer_1 (
    .in0(32'he1), .in1(subtractor_1_out), .out(multiplexer_1_out), .sel(rom_1_data[2]), .en(rom_1_data[3]));
  Register #(.width(32)) register_1 (.D(multiplexer_1_out), .Q(register_1_q), .clk(C));  // open: en, clr
  Comparator #(.width(32)) comparator_1 (.a(register_1_q), .b(register_2_q), .lt(comparator_1_lt[0]));  // open: gt, eq
  ROM #(.addrWidth(5), .dataWidth(6)) rom_1 (.addr(comparator_1_lt), .data(rom_1_data));  // open: sel
  D_Flip_Flop d_ff_1 (.clk(C), .D(rom_1_data[5]), .Q(comparator_1_lt[4]));  // open: Qn, preset, en, reset
  D_Flip_Flop d_ff_2 (.clk(C), .D(rom_1_data[4]), .Q(comparator_1_lt[3]));  // open: Qn, preset, en, reset
  Clock Master_clock (.out(C));
  Register #(.width(32)) register_2 (.D(32'ha), .Q(register_2_q), .clk(C));  // open: en, clr
  Button Single_step ();  // open: out
  Adder #(.width(32)) adder_1 (.a(register_3_q), .b(32'h1), .out(adder_1_out));  // open: cin, cout
  Multiplexer #(.width(32)) multiplexer_2 (
    .in0({32{1'b0}}), .in1(adder_1_out), .out(multiplexer_2_out), .sel(rom_1_data[0]), .en(rom_1_data[1]));
  Register #(.width(32)) register_3 (.D(multiplexer_2_out), .Q(register_3_q), .clk(C));  // open: en, clr

  // Notes on the sheet:
  //   a
  //   a<b
  //   contents of rom_1 (hex, n*v repeats v):
  //   4*0 1a 1a 0 0 1f 30 0 5*10 8*0 30 30 30 0 4*30
  //   b
  //   x
endmodule
